# Fritzing sketch connections (saved by Fritzing 0.9.2b)

parts:
  U2 = NodeMCU V1.0
  J1 = ATX24 Pin Power Supply Connector [package=atx24_right_angle]

nets:
  GND: U2.D2, U2.GND, J1.GND, J1.PS_ON
  N1: U2.D3, J1.PWR_OK
  VIN: U2.Vin, J1.5V_STDBY, J1.12V

custom parts:
  NodeMCU V1.0: ESP8266 based NodeMCU
